# Fritzing sketch self_driving_car_1 (saved by Fritzing 0.9.3b)

parts:
  Part1 = Arduino Uno (Rev3)
  hc-sr1 = hc-sr04
  BAT1 = BC9VPC [package=bc9vpc]
  S1 = H-Bridge with L298N
  M1 = DC Motor

nets:
  GND: Part1.GND, hc-sr1.GND, BAT1.V+, S1.GND
  N1: Part1.D2, hc-sr1.Trig
  N2: Part1.D3_PWM, hc-sr1.Echo
  N3: Part1.D4, S1.IN4
  N4: Part1.D5_PWM, S1.IN3
  5V: Part1.5V, hc-sr1.VCC
  N5: BAT1.V-, S1.12V
  N6: S1.M2-01, M1.pin_2
  N7: S1.M2-02, M1.pin_1

custom parts:
  H-Bridge with L298N: h-bridge
